# Fritzing sketch Display Sensor Values on LCD (saved by Fritzing 0.5.2b)
breadboards: 1

parts:
  LCD1 = LCD screen
  Arduino1 = Arduino
  R1 = Rotary Potentiometer (Small)
  R2 = Trimmer Potentiometer [package=THT]
  R3 = Trimmer Potentiometer [package=THT]

nets (from the breadboard view):
  VSS: LCD1.VSS, LCD1.R/W, LCD1.LED-, Arduino1.GND, R1.leg1, R2.leg2, R3.leg2
  VDD: LCD1.VDD, LCD1.LED+, Arduino1.+5V, R1.leg2, R2.leg1, R3.leg1
  N1: LCD1.V0, R1.wiper
  N2: LCD1.RS, Arduino1.D7
  N3: LCD1.E, Arduino1.D8
  N4: LCD1.DB4, Arduino1.D9
  N5: LCD1.DB5, Arduino1.D10
  N6: LCD1.DB6, Arduino1.D11
  N7: LCD1.DB7, Arduino1.D12
  N8: Arduino1.A1, R2.wiper
  N9: Arduino1.A2, R3.wiper

notes:
  Black Wire = ground
  Red Wire = power
  Green Wire = wiper on contrast Pot
  Yellow Wire = bus wire
  White Wire = wiper on trim pots
