# Fritzing sketch MenuForMonoLCDsch (saved by Fritzing 0.5.2b)
breadboards: 1

parts:
  Arduino1 = Arduino
  LCD1 = LCD screen
  R1 = Rotary Potentiometer (Small)
  R2 = Trimmer Potentiometer [package=THT]
  R3 = Trimmer Potentiometer [package=THT]
  S1 = Pushbutton [package=THT]

nets:
  N1: Arduino1.D12, LCD1.DB7
  N2: Arduino1.D11, LCD1.DB6
  N3: Arduino1.D10, LCD1.DB5
  N4: Arduino1.D9, LCD1.DB4
  N5: Arduino1.D8, LCD1.E
  N6: Arduino1.D7, LCD1.RS
  N7: Arduino1.D2, S1.leg0
  +5V: Arduino1.+5V, LCD1.VDD, LCD1.LED+, R1.leg2, R2.leg1, R3.leg1
  GND: Arduino1.GND, LCD1.VSS, LCD1.R/W, LCD1.LED-, R1.leg1, R2.leg2, R3.leg2, S1.leg1
  N8: Arduino1.A1, R2.wiper
  N9: Arduino1.A2, R3.wiper
  N10: LCD1.V0, R1.wiper

notes:
  Black Wire = ground
  Red Wire = power
  Green Wire = wiper on contrast Pot
  Yellow Wire = bus wire
  White Wire = wiper on trim pots
  Orange Wire = push button
